# Fritzing sketch pump automation (saved by Fritzing 0.9.3b)

parts:
  Part1 = Arduino Uno (Rev3)
  LCD1 = LCD screen
  R1 = Trimmer Potentiometer [maximum_resistance=10kΩ package=THT]
  R2 = Trimmer Potentiometer [maximum_resistance=10kΩ package=THT]
  Q1 = NPN-Transistor [package="SOT-23 [SMD]"]  # not connected
  R3 = Resistor [tolerance=±5% resistance=220 package="0402 [SMD]"]
  S1 = Momentary Switch [package=ksa_sealed_tac_switch]
  S2 = Momentary Switch [package=ksa_sealed_tac_switch]
  R4 = Resistor [tolerance=±5% resistance=220 package=THT]
  Mod1 = KY-019 5V Relay Module [package="Breakout board"]

nets:
  N1: Part1.D8, S1.3
  N2: Part1.D10_PWM/SS, S2.3
  N3: Part1.D11_PWM/MOSI, LCD1.E
  N4: Part1.D12/MISO, LCD1.RS
  N5: Part1.GND, LCD1.R/W, LCD1.LED-, R2.leg1, R4.Pin_0, Mod1.-
  N6: Part1.D2, LCD1.DB7
  N7: Part1.D3_PWM, LCD1.DB6
  N8: Part1.D4, LCD1.DB5
  N9: Part1.D5_PWM, LCD1.DB4
  N10: Part1.D6_PWM, Mod1.S
  N11: Part1.D7, R3.Pin_0
  5V: Part1.5V, LCD1.VDD, S1.2
  N12: LCD1.VSS, R1.leg1
  N13: LCD1.V0, R1.wiper
  N14: LCD1.LED+, R2.wiper
  N15: R1.leg2, R3.Pin_1, Mod1.+
  N16: S1.4, S2.4, R4.Pin_1

custom parts:
  KY-019 5V Relay Module: KY-019 5V Relay module, used to control AC circuits. (Special thanks to vanepp for fixing the PCB holes and other errors)
